// Logisim project Main.circ as structural Verilog: 7 circuits, main circuit main
module main (
);

  wire _1_out, _2_out, _3_out, _4_2_out, _4_out, _5_2_out, _5_out, _6_2_out, _6_out, _7_out, _8_out,
       ai_move_2_out_6, ai_move_3_out_6, ai_move_4_out_6, ai_move_5_out_6, ai_move_6_out_6, AI_out, btn_flag,
       button_driver_1_trigger, Calculate_Holes, Choose_Setts, Cl, clear_btn_reg, Computing,
       display_driver_2_is_zero, display_driver_2_out_13, display_driver_2_out_14, display_driver_3_out_13,
       display_driver_3_out_14, display_driver_4_out_13, display_driver_4_out_14, display_driver_5_out_13,
       display_driver_5_out_14, display_driver_6_out_13, display_driver_6_out_14, display_driver_7_out_13,
       display_driver_7_out_14, display_driver_8_out_13, display_driver_8_out_14, display_driver_9_out_13,
       display_driver_9_out_14, display_driver_10_out_13, display_driver_10_out_14, display_driver_11_out_13,
       display_driver_11_out_14, display_driver_12_out_13, display_driver_12_out_14,
       display_driver_13_out_13, display_driver_13_out_14, display_driver_14_out_13,
       display_driver_14_out_14, Error, game_operator_1_out_7, game_operator_1_out_8, game_operator_1_w_r,
       GAME_OVER, MemDat, pull_resistor_1_node, RAM, rd_wr_prime, start_seeds_1_out_11, start_seeds_1_out_12,
       start_seeds_1_out_13, Wait_Move, wld_fl, You_out;
  wire [3:0] display_driver_1_tens, display_driver_1_units, display_driver_2_tens, display_driver_2_units,
       display_driver_3_tens, display_driver_3_units, display_driver_4_tens, display_driver_4_units,
       display_driver_5_tens, display_driver_5_units, display_driver_6_tens, display_driver_6_units,
       display_driver_7_tens, display_driver_7_units, display_driver_8_tens, display_driver_8_units,
       display_driver_9_tens, display_driver_9_units, display_driver_10_tens, display_driver_10_units,
       display_driver_11_tens, display_driver_11_units, display_driver_12_tens, display_driver_12_units,
       display_driver_13_tens, display_driver_13_units, display_driver_14_tens, display_driver_14_units;
  wire [4:0] ai_move_1_move, ai_move_1_out_9, ai_move_1_out_10, ai_move_1_out_12, ai_move_1_out_13,
       ai_move_2_move, ai_move_2_out_9, ai_move_2_out_10, ai_move_2_out_12, ai_move_2_out_13, ai_move_3_move,
       ai_move_3_out_9, ai_move_3_out_10, ai_move_3_out_12, ai_move_3_out_13, ai_move_4_move,
       ai_move_4_out_9, ai_move_4_out_10, ai_move_4_out_12, ai_move_4_out_13, ai_move_5_move,
       ai_move_5_out_9, ai_move_5_out_10, ai_move_5_out_12, ai_move_5_out_13, ai_move_6_move,
       ai_move_6_out_9, ai_move_6_out_10, ai_move_6_out_12, ai_move_6_out_13;
  wire [7:0] ai_move_2_chain_addr_out, ai_move_2_out_5, ai_move_2_out_8, ai_move_3_chain_addr_out,
       ai_move_3_out_5, ai_move_3_out_8, ai_move_4_chain_addr_out, ai_move_4_out_5, ai_move_4_out_8,
       ai_move_5_chain_addr_out, ai_move_5_out_5, ai_move_5_out_8, ai_move_6_chain_addr_out, ai_move_6_out_5,
       ai_move_6_out_8, button_driver_1_addr_out, button_driver_2_addr_out, button_driver_3_addr_out,
       button_driver_4_addr_out, button_driver_5_addr_out, button_driver_6_addr_out, Data,
       display_driver_2_addr_field_2, display_driver_2_chain_addr_out, display_driver_2_ram_data_out,
       display_driver_3_addr_field_2, display_driver_3_chain_addr_out, display_driver_3_ram_data_out,
       display_driver_4_addr_field_2, display_driver_4_chain_addr_out, display_driver_4_ram_data_out,
       display_driver_4_self_addr, display_driver_5_addr_field_2, display_driver_5_chain_addr_out,
       display_driver_5_ram_data_out, display_driver_6_addr_field_2, display_driver_6_chain_addr_out,
       display_driver_6_ram_data_out, display_driver_6_self_addr, display_driver_7_addr_field_2,
       display_driver_7_chain_addr_out, display_driver_7_ram_data_out, display_driver_8_addr_field_2,
       display_driver_8_chain_addr_out, display_driver_8_ram_data_out, display_driver_8_self_addr,
       display_driver_9_addr_field_2, display_driver_9_chain_addr_out, display_driver_9_ram_data_out,
       display_driver_10_addr_field_2, display_driver_10_chain_addr_out, display_driver_10_ram_data_out,
       display_driver_10_self_addr, display_driver_11_addr_field_2, display_driver_11_chain_addr_out,
       display_driver_11_ram_data_out, display_driver_12_addr_field_2, display_driver_12_chain_addr_out,
       display_driver_12_ram_data_out, display_driver_12_self_addr, display_driver_13_addr_field_2,
       display_driver_13_chain_addr_out, display_driver_13_ram_data_out, display_driver_13_self_addr,
       display_driver_14_addr_field_2, display_driver_14_chain_addr_out, display_driver_14_ram_data_out,
       game_operator_1_out_4, increment_1_value_out, Proc_addr, start_seeds_1_address_2, start_seeds_1_value,
       Value;

  Hex_Digit_Display hex_digit_display_1 (.value(display_driver_1_units));  // open: dp
  Hex_Digit_Display hex_digit_display_2 (.value(display_driver_1_tens));  // open: dp
  Display_driver display_driver_1 (
    .addr_field(display_driver_2_addr_field_2), .chain_addr_in(display_driver_2_chain_addr_out),
    .ram_data_in(display_driver_2_ram_data_out), .Cl(display_driver_2_out_13), .tens(display_driver_1_tens),
    .units(display_driver_1_units), .ram_flag(display_driver_2_out_14));  // open: addr_field_2, chain_addr_out, ram_data_out, is_zero, self_addr, out_13, out_14
  WLD wld_1 (
    .out_7(wld_fl), .End(display_driver_2_is_zero), .Address(Proc_addr), .DatMem(MemDat), .Clock(Cl),
    .Write_Read(rd_wr_prime), .Data(Value), .Doc_Cell(8'h16));
  Display_driver display_driver_2 (
    .addr_field(display_driver_3_addr_field_2), .chain_addr_in(display_driver_3_chain_addr_out),
    .ram_data_in(display_driver_3_ram_data_out), .Cl(display_driver_3_out_13),
    .addr_field_2(display_driver_2_addr_field_2), .chain_addr_out(display_driver_2_chain_addr_out),
    .ram_data_out(display_driver_2_ram_data_out), .tens(display_driver_2_tens),
    .units(display_driver_2_units), .is_zero(display_driver_2_is_zero), .ram_flag(display_driver_3_out_14),
    .out_13(display_driver_2_out_13), .out_14(display_driver_2_out_14));  // open: self_addr
  User_move user_move_1 (
    .wr_id_cell(Value), .id_cell(button_driver_1_addr_out), .bttn_pressed(button_driver_1_trigger),
    .clock(Cl), .MemDat(MemDat), .wait_move(Wait_Move), .ProcAdr(Proc_addr), .need_clear(clear_btn_reg),
    .need_write(btn_flag));
  Messages messages_1 (
    .RAM_val(Data), .in_2(Proc_addr), .in_3(Cl), .in_4(MemDat), .mes(Error), .mes_2(clear_btn_reg),
    .mes_3(Choose_Setts), .mes_4(Wait_Move), .mes_5(Computing), .mes_6(Calculate_Holes), .mes_7(GAME_OVER));  // open: mes_8
  DotMatrix #(.matrixrows(5), .persist(275)) dotmatrix_1 (
    .col0(ai_move_1_out_9), .col1(ai_move_1_out_12), .col2(ai_move_1_move), .col3(ai_move_1_out_13),
    .col4(ai_move_1_out_10));
  Hex_Digit_Display hex_digit_display_3 (.value(display_driver_2_tens));  // open: dp
  Hex_Digit_Display hex_digit_display_4 (.value(display_driver_4_tens));  // open: dp
  Hex_Digit_Display hex_digit_display_5 (.value(display_driver_4_units));  // open: dp
  Button _1 (.out(_1_out));
  DotMatrix #(.matrixrows(5), .persist(275)) dotmatrix_2 (
    .col0(ai_move_2_out_9), .col1(ai_move_2_out_12), .col2(ai_move_2_move), .col3(ai_move_2_out_13),
    .col4(ai_move_2_out_10));
  AI_move ai_move_1 (
    .proc_addr(ai_move_2_out_5), .ram_flag(ai_move_2_out_6), .chain_addr_in(ai_move_2_chain_addr_out),
    .ram_data_in(ai_move_2_out_8), .Move(ai_move_1_move), .out_12(ai_move_1_out_12),
    .out_13(ai_move_1_out_13), .out_9(ai_move_1_out_9), .out_10(ai_move_1_out_10));  // open: out_5, out_6, chain_addr_out, out_8
  Display_driver display_driver_3 (
    .addr_field(display_driver_5_addr_field_2), .chain_addr_in(display_driver_5_chain_addr_out),
    .ram_data_in(display_driver_5_ram_data_out), .Cl(display_driver_5_out_13),
    .addr_field_2(display_driver_3_addr_field_2), .chain_addr_out(display_driver_3_chain_addr_out),
    .ram_data_out(display_driver_3_ram_data_out), .tens(display_driver_3_tens),
    .units(display_driver_3_units), .is_zero(display_driver_2_is_zero), .ram_flag(display_driver_5_out_14),
    .out_13(display_driver_3_out_13), .out_14(display_driver_3_out_14));  // open: self_addr
  Hex_Digit_Display hex_digit_display_6 (.value(display_driver_2_units));  // open: dp
  LED led_1 (.in(Choose_Setts));
  LED led_2 (.in(Choose_Setts));
  LED led_3 (.in(Choose_Setts));
  Pull_Resistor #(.pull(1)) pull_resistor_1 (.node(pull_resistor_1_node));
  Hex_Digit_Display hex_digit_display_7 (.value(display_driver_6_tens));  // open: dp
  Display_driver display_driver_4 (
    .addr_field(Proc_addr), .chain_addr_in({8{1'b0}}), .ram_data_in(Data), .Cl(Cl),
    .addr_field_2(display_driver_4_addr_field_2), .chain_addr_out(display_driver_4_chain_addr_out),
    .ram_data_out(display_driver_4_ram_data_out), .tens(display_driver_4_tens),
    .units(display_driver_4_units), .is_zero(pull_resistor_1_node), .self_addr(display_driver_4_self_addr),
    .ram_flag(MemDat), .out_13(display_driver_4_out_13), .out_14(display_driver_4_out_14));
  Button_driver button_driver_1 (
    .addr_out(button_driver_1_addr_out), .addr_in(button_driver_2_addr_out),
    .pos(display_driver_4_self_addr), .button(_1_out), .trigger(button_driver_1_trigger));
  AI_move ai_move_2 (
    .proc_addr(ai_move_3_out_5), .ram_flag(ai_move_3_out_6), .chain_addr_in(ai_move_3_chain_addr_out),
    .ram_data_in(ai_move_3_out_8), .out_5(ai_move_2_out_5), .out_6(ai_move_2_out_6),
    .chain_addr_out(ai_move_2_chain_addr_out), .Move(ai_move_2_move), .out_8(ai_move_2_out_8),
    .out_12(ai_move_2_out_12), .out_13(ai_move_2_out_13), .out_9(ai_move_2_out_9), .out_10(ai_move_2_out_10));
  Display_driver display_driver_5 (
    .addr_field(display_driver_7_addr_field_2), .chain_addr_in(display_driver_7_chain_addr_out),
    .ram_data_in(display_driver_7_ram_data_out), .Cl(display_driver_7_out_13),
    .addr_field_2(display_driver_5_addr_field_2), .chain_addr_out(display_driver_5_chain_addr_out),
    .ram_data_out(display_driver_5_ram_data_out), .tens(display_driver_5_tens),
    .units(display_driver_5_units), .is_zero(display_driver_2_is_zero), .ram_flag(display_driver_7_out_14),
    .out_13(display_driver_5_out_13), .out_14(display_driver_5_out_14));  // open: self_addr
  Hex_Digit_Display hex_digit_display_8 (.value(display_driver_3_units));  // open: dp
  Hex_Digit_Display hex_digit_display_9 (.value(display_driver_3_tens));  // open: dp
  LED led_4 (.in(Choose_Setts));
  LED led_5 (.in(Choose_Setts));
  LED led_6 (.in(Computing));
  Hex_Digit_Display hex_digit_display_10 (.value(display_driver_6_units));  // open: dp
  Button _2 (.out(_2_out));
  Clock clock_1 (.out(Cl));
  DotMatrix #(.matrixrows(5), .persist(275)) dotmatrix_3 (
    .col0(ai_move_3_out_9), .col1(ai_move_3_out_12), .col2(ai_move_3_move), .col3(ai_move_3_out_13),
    .col4(ai_move_3_out_10));
  Hex_Digit_Display hex_digit_display_11 (.value(display_driver_5_tens));  // open: dp
  LED led_7 (.in(Computing));
  LED led_8 (.in(Computing));
  LED led_9 (.in(Computing));
  LED led_10 (.in(Computing));
  Display_driver display_driver_6 (
    .addr_field(display_driver_4_addr_field_2), .chain_addr_in(display_driver_4_chain_addr_out),
    .ram_data_in(display_driver_4_ram_data_out), .Cl(display_driver_4_out_13),
    .addr_field_2(display_driver_6_addr_field_2), .chain_addr_out(display_driver_6_chain_addr_out),
    .ram_data_out(display_driver_6_ram_data_out), .tens(display_driver_6_tens),
    .units(display_driver_6_units), .is_zero(pull_resistor_1_node), .self_addr(display_driver_6_self_addr),
    .ram_flag(display_driver_4_out_14), .out_13(display_driver_6_out_13), .out_14(display_driver_6_out_14));
  Hex_Digit_Display hex_digit_display_12 (.value(display_driver_8_units));  // open: dp
  Hex_Digit_Display hex_digit_display_13 (.value(display_driver_8_tens));  // open: dp
  Button_driver button_driver_2 (
    .addr_out(button_driver_2_addr_out), .addr_in(button_driver_3_addr_out),
    .pos(display_driver_6_self_addr), .button(_2_out), .trigger(button_driver_1_trigger));
  Button _3 (.out(_3_out));
  AI_move ai_move_3 (
    .proc_addr(ai_move_4_out_5), .ram_flag(ai_move_4_out_6), .chain_addr_in(ai_move_4_chain_addr_out),
    .ram_data_in(ai_move_4_out_8), .out_5(ai_move_3_out_5), .out_6(ai_move_3_out_6),
    .chain_addr_out(ai_move_3_chain_addr_out), .Move(ai_move_3_move), .out_8(ai_move_3_out_8),
    .out_12(ai_move_3_out_12), .out_13(ai_move_3_out_13), .out_9(ai_move_3_out_9), .out_10(ai_move_3_out_10));
  DotMatrix #(.matrixrows(5), .persist(275)) dotmatrix_4 (
    .col0(ai_move_4_out_9), .col1(ai_move_4_out_12), .col2(ai_move_4_move), .col3(ai_move_4_out_13),
    .col4(ai_move_4_out_10));
  Display_driver display_driver_7 (
    .addr_field(display_driver_9_addr_field_2), .chain_addr_in(display_driver_9_chain_addr_out),
    .ram_data_in(display_driver_9_ram_data_out), .Cl(display_driver_9_out_13),
    .addr_field_2(display_driver_7_addr_field_2), .chain_addr_out(display_driver_7_chain_addr_out),
    .ram_data_out(display_driver_7_ram_data_out), .tens(display_driver_7_tens),
    .units(display_driver_7_units), .is_zero(display_driver_2_is_zero), .ram_flag(display_driver_9_out_14),
    .out_13(display_driver_7_out_13), .out_14(display_driver_7_out_14));  // open: self_addr
  Hex_Digit_Display hex_digit_display_14 (.value(display_driver_5_units));  // open: dp
  LED led_11 (.in(GAME_OVER));
  LED led_12 (.in(GAME_OVER));
  LED led_13 (.in(GAME_OVER));
  LED led_14 (.in(Wait_Move));
  LED led_15 (.in(Wait_Move));
  LED led_16 (.in(Wait_Move));
  Display_driver display_driver_8 (
    .addr_field(display_driver_6_addr_field_2), .chain_addr_in(display_driver_6_chain_addr_out),
    .ram_data_in(display_driver_6_ram_data_out), .Cl(display_driver_6_out_13),
    .addr_field_2(display_driver_8_addr_field_2), .chain_addr_out(display_driver_8_chain_addr_out),
    .ram_data_out(display_driver_8_ram_data_out), .tens(display_driver_8_tens),
    .units(display_driver_8_units), .is_zero(pull_resistor_1_node), .self_addr(display_driver_8_self_addr),
    .ram_flag(display_driver_6_out_14), .out_13(display_driver_8_out_13), .out_14(display_driver_8_out_14));
  Hex_Digit_Display hex_digit_display_15 (.value(display_driver_10_tens));  // open: dp
  Button_driver button_driver_3 (
    .addr_out(button_driver_3_addr_out), .addr_in(button_driver_4_addr_out),
    .pos(display_driver_8_self_addr), .button(_3_out), .trigger(button_driver_1_trigger));
  AI_move ai_move_4 (
    .proc_addr(ai_move_5_out_5), .ram_flag(ai_move_5_out_6), .chain_addr_in(ai_move_5_chain_addr_out),
    .ram_data_in(ai_move_5_out_8), .out_5(ai_move_4_out_5), .out_6(ai_move_4_out_6),
    .chain_addr_out(ai_move_4_chain_addr_out), .Move(ai_move_4_move), .out_8(ai_move_4_out_8),
    .out_12(ai_move_4_out_12), .out_13(ai_move_4_out_13), .out_9(ai_move_4_out_9), .out_10(ai_move_4_out_10));
  Display_driver display_driver_9 (
    .addr_field(display_driver_11_addr_field_2), .chain_addr_in(display_driver_11_chain_addr_out),
    .ram_data_in(display_driver_11_ram_data_out), .Cl(display_driver_11_out_13),
    .addr_field_2(display_driver_9_addr_field_2), .chain_addr_out(display_driver_9_chain_addr_out),
    .ram_data_out(display_driver_9_ram_data_out), .tens(display_driver_9_tens),
    .units(display_driver_9_units), .is_zero(display_driver_2_is_zero), .ram_flag(display_driver_11_out_14),
    .out_13(display_driver_9_out_13), .out_14(display_driver_9_out_14));  // open: self_addr
  Hex_Digit_Display hex_digit_display_16 (.value(display_driver_7_tens));  // open: dp
  Hex_Digit_Display hex_digit_display_17 (.value(display_driver_7_units));  // open: dp
  LED led_17 (.in(GAME_OVER));
  LED led_18 (.in(GAME_OVER));
  LED led_19 (.in(Wait_Move));
  LED led_20 (.in(Wait_Move));
  LED led_21 (.in(Error));
  Hex_Digit_Display hex_digit_display_18 (.value(display_driver_10_units));  // open: dp
  Button _4 (.out(_4_out));
  Game_operator game_operator_1 (
    .Cl(Cl), .InputData(Value), .out_4(game_operator_1_out_4), .out_5(Data), .out_8(game_operator_1_out_8),
    .W_R(game_operator_1_w_r), .RAM(RAM), .out_7(game_operator_1_out_7));
  Button _6 (.out(_6_out));
  Button _4_2 (.out(_4_2_out));
  Button _5 (.out(_5_out));
  DotMatrix #(.matrixrows(5), .persist(275)) dotmatrix_5 (
    .col0(ai_move_5_out_9), .col1(ai_move_5_out_12), .col2(ai_move_5_move), .col3(ai_move_5_out_13),
    .col4(ai_move_5_out_10));
  Hex_Digit_Display hex_digit_display_19 (.value(display_driver_9_tens));  // open: dp
  LED led_22 (.in(Error));
  LED led_23 (.in(Error));
  LED led_24 (.in(Error));
  LED led_25 (.in(Error));
  Hex_Digit_Display hex_digit_display_20 (.value(display_driver_12_tens));  // open: dp
  Display_driver display_driver_10 (
    .addr_field(display_driver_8_addr_field_2), .chain_addr_in(display_driver_8_chain_addr_out),
    .ram_data_in(display_driver_8_ram_data_out), .Cl(display_driver_8_out_13),
    .addr_field_2(display_driver_10_addr_field_2), .chain_addr_out(display_driver_10_chain_addr_out),
    .ram_data_out(display_driver_10_ram_data_out), .tens(display_driver_10_tens),
    .units(display_driver_10_units), .is_zero(pull_resistor_1_node), .self_addr(display_driver_10_self_addr),
    .ram_flag(display_driver_8_out_14), .out_13(display_driver_10_out_13), .out_14(display_driver_10_out_14));
  Hex_Digit_Display hex_digit_display_21 (.value(display_driver_12_units));  // open: dp
  Button_driver button_driver_4 (
    .addr_out(button_driver_4_addr_out), .addr_in(button_driver_5_addr_out),
    .pos(display_driver_10_self_addr), .button(_4_out), .trigger(button_driver_1_trigger));
  Button _5_2 (.out(_5_2_out));
  Start_Seeds start_seeds_1 (
    .Address(game_operator_1_out_4), .StFlag(game_operator_1_out_8), .Clock(game_operator_1_out_7),
    .Write_Read(game_operator_1_w_r), .Value(start_seeds_1_value), ._4(_4_2_out), ._5(_5_out), ._6(_6_out),
    ._7(_7_out), ._8(_8_out), .out_13(start_seeds_1_out_13), .out_12(start_seeds_1_out_12),
    .Address_2(start_seeds_1_address_2), .out_11(start_seeds_1_out_11));
  Button _8 (.out(_8_out));
  Button _7 (.out(_7_out));
  DotMatrix #(.matrixrows(5), .persist(275)) dotmatrix_6 (
    .col0(ai_move_6_out_9), .col1(ai_move_6_out_12), .col2(ai_move_6_move), .col3(ai_move_6_out_13),
    .col4(ai_move_6_out_10));
  AI_move ai_move_5 (
    .proc_addr(ai_move_6_out_5), .ram_flag(ai_move_6_out_6), .chain_addr_in(ai_move_6_chain_addr_out),
    .ram_data_in(ai_move_6_out_8), .out_5(ai_move_5_out_5), .out_6(ai_move_5_out_6),
    .chain_addr_out(ai_move_5_chain_addr_out), .Move(ai_move_5_move), .out_8(ai_move_5_out_8),
    .out_12(ai_move_5_out_12), .out_13(ai_move_5_out_13), .out_9(ai_move_5_out_9), .out_10(ai_move_5_out_10));
  Display_driver display_driver_11 (
    .addr_field(display_driver_14_addr_field_2), .chain_addr_in(increment_1_value_out),
    .ram_data_in(display_driver_14_ram_data_out), .Cl(display_driver_14_out_13),
    .addr_field_2(display_driver_11_addr_field_2), .chain_addr_out(display_driver_11_chain_addr_out),
    .ram_data_out(display_driver_11_ram_data_out), .tens(display_driver_11_tens),
    .units(display_driver_11_units), .is_zero(display_driver_2_is_zero), .ram_flag(display_driver_14_out_14),
    .out_13(display_driver_11_out_13), .out_14(display_driver_11_out_14));  // open: self_addr
  Hex_Digit_Display hex_digit_display_22 (.value(display_driver_9_units));  // open: dp
  Pull_Resistor #(.pull(1)) pull_resistor_2 (.node(display_driver_2_is_zero));
  LED led_26 (.in(Calculate_Holes));
  LED led_27 (.in(Calculate_Holes));
  LED led_28 (.in(Calculate_Holes));
  Display_driver display_driver_12 (
    .addr_field(display_driver_10_addr_field_2), .chain_addr_in(display_driver_10_chain_addr_out),
    .ram_data_in(display_driver_10_ram_data_out), .Cl(display_driver_10_out_13),
    .addr_field_2(display_driver_12_addr_field_2), .chain_addr_out(display_driver_12_chain_addr_out),
    .ram_data_out(display_driver_12_ram_data_out), .tens(display_driver_12_tens),
    .units(display_driver_12_units), .is_zero(pull_resistor_1_node), .self_addr(display_driver_12_self_addr),
    .ram_flag(display_driver_10_out_14), .out_13(display_driver_12_out_13), .out_14(display_driver_12_out_14));
  Hex_Digit_Display hex_digit_display_23 (.value(display_driver_13_tens));  // open: dp
  Button_driver button_driver_5 (
    .addr_out(button_driver_5_addr_out), .addr_in(button_driver_6_addr_out),
    .pos(display_driver_12_self_addr), .button(_5_2_out), .trigger(button_driver_1_trigger));
  Button You (.out(You_out));
  Button AI (.out(AI_out));
  AI_move ai_move_6 (
    .proc_addr(Proc_addr), .ram_flag(RAM), .chain_addr_in(8'h9), .ram_data_in(Data), .out_5(ai_move_6_out_5),
    .out_6(ai_move_6_out_6), .chain_addr_out(ai_move_6_chain_addr_out), .Move(ai_move_6_move),
    .out_8(ai_move_6_out_8), .out_12(ai_move_6_out_12), .out_13(ai_move_6_out_13), .out_9(ai_move_6_out_9),
    .out_10(ai_move_6_out_10));
  Hex_Digit_Display hex_digit_display_24 (.value(display_driver_11_tens));  // open: dp
  Hex_Digit_Display hex_digit_display_25 (.value(display_driver_11_units));  // open: dp
  LED led_29 (.in(Calculate_Holes));
  LED led_30 (.in(Calculate_Holes));
  Hex_Digit_Display hex_digit_display_26 (.value(display_driver_13_units));  // open: dp
  Pull_Resistor pull_resistor_3 (.node(button_driver_1_trigger));
  Button _6_2 (.out(_6_2_out));
  First_move first_move_1 (
    .Address(start_seeds_1_address_2), .StFlag(start_seeds_1_out_11), .Clock(start_seeds_1_out_12),
    .Write_Read(start_seeds_1_out_13), .AI(AI_out), .User(You_out), .out_8(Proc_addr), .out_10(rd_wr_prime),
    .out_9(MemDat), .Data(start_seeds_1_value), .Value(Value));
  Increment increment_1 (.value_in(display_driver_14_chain_addr_out), .value_out(increment_1_value_out));
  Display_driver display_driver_13 (
    .addr_field(display_driver_12_addr_field_2), .chain_addr_in(display_driver_12_chain_addr_out),
    .ram_data_in(display_driver_12_ram_data_out), .Cl(display_driver_12_out_13),
    .addr_field_2(display_driver_13_addr_field_2), .chain_addr_out(display_driver_13_chain_addr_out),
    .ram_data_out(display_driver_13_ram_data_out), .tens(display_driver_13_tens),
    .units(display_driver_13_units), .is_zero(pull_resistor_1_node), .self_addr(display_driver_13_self_addr),
    .ram_flag(display_driver_12_out_14), .out_13(display_driver_13_out_13), .out_14(display_driver_13_out_14));
  Button_driver button_driver_6 (
    .addr_out(button_driver_6_addr_out), .pos(display_driver_13_self_addr), .button(_6_2_out),
    .trigger(button_driver_1_trigger));  // open: addr_in
  and and_1 (RAM, MemDat, ~btn_flag, wld_fl);  // AND_Gate
  WLD wld_2 (
    .out_7(wld_fl), .End(pull_resistor_1_node), .Address(Proc_addr), .DatMem(MemDat), .Clock(Cl),
    .Write_Read(rd_wr_prime), .Data(Value), .Doc_Cell(8'h17));
  Display_driver display_driver_14 (
    .addr_field(display_driver_13_addr_field_2), .chain_addr_in(display_driver_13_chain_addr_out),
    .ram_data_in(display_driver_13_ram_data_out), .Cl(display_driver_13_out_13),
    .addr_field_2(display_driver_14_addr_field_2), .chain_addr_out(display_driver_14_chain_addr_out),
    .ram_data_out(display_driver_14_ram_data_out), .tens(display_driver_14_tens),
    .units(display_driver_14_units), .ram_flag(display_driver_13_out_14), .out_13(display_driver_14_out_13),
    .out_14(display_driver_14_out_14));  // open: is_zero, self_addr
  Hex_Digit_Display hex_digit_display_27 (.value(display_driver_14_units));  // open: dp
  Hex_Digit_Display hex_digit_display_28 (.value(display_driver_14_tens));  // open: dp
endmodule

module User_move (
  input  [7:0] id_cell,
  input  bttn_pressed,
  input  [7:0] ProcAdr,
  input  clock,
  input  need_clear,
  input  MemDat,
  input  wait_move,
  output [7:0] wr_id_cell,
  output need_write
);

  wire [7:0] register_1_q;

  assign wr_id_cell = need_write ? register_1_q : 8'bz;  // Controlled_Buffer controlled_buffer_1
  Flag_base flag_base_1 (.proc_addr(ProcAdr), .need_addr(8'h15), .cond1(MemDat), .cond2(wait_move), .flag(need_write));
  Register register_1 (.D(id_cell), .en(bttn_pressed), .Q(register_1_q), .clk(clock), .clr(need_clear));
endmodule

module Flag_base (
  input  [7:0] proc_addr,
  input  [7:0] need_addr,
  input  cond1,
  input  cond2,
  output flag
);

  wire comparator_1_eq;

  Comparator comparator_1 (.a(proc_addr), .b(need_addr), .eq(comparator_1_eq));  // open: gt, lt
  and and_1 (flag, comparator_1_eq, cond1, cond2);
endmodule

module Messages (
  input  [7:0] RAM_val,
  input  [7:0] in_2,
  input  in_3,
  input  in_4,
  output mes,
  output mes_2,
  output mes_3,
  output mes_4,
  output mes_5,
  output mes_6,
  output mes_7,
  output mes_8
);

  wire flag_base_1_flag;

  Flag_base flag_base_1 (.proc_addr(in_2), .need_addr(8'h12), .cond1(in_3), .cond2(in_4), .flag(flag_base_1_flag));
  Register register_1 (
    .D(RAM_val), .Q({mes_8, mes_7, mes_6, mes_5, mes_4, mes_3, mes_2, mes}), .clk(flag_base_1_flag));  // open: en, clr
endmodule

module Bank_switch (
  input  CodeFlag,
  input  [7:0] Data,
  input  [7:0] in_3,
  input  Storage_flag,
  input  Cl,
  output MoveMaker,
  output User,
  output Deep_Purple,
  output Main
);

  wire flag_base_1_flag;
  wire [1:0] register_1_q;

  Flag_base flag_base_1 (
    .proc_addr(in_3), .need_addr(8'h11), .cond2(Storage_flag), .flag(flag_base_1_flag));  // open: cond1
  Register #(.width(2)) register_1 (.D(Data[1:0]), .en(flag_base_1_flag), .Q(register_1_q), .clk(Cl));  // open: clr
  Decoder #(.select(2), .disabled(0)) decoder_1 (
    .out0(Main), .out1(Deep_Purple), .out2(User), .out3(MoveMaker), .sel(register_1_q), .en(CodeFlag));
endmodule

module Game_operator (
  input  Cl,
  input  [7:0] InputData,
  input  RAM,
  output [7:0] out_4,
  output [7:0] out_5,
  output W_R,
  output out_7,
  output out_8
);

  wire cdm_8_mark5_1_p1, cdm_8_mark5_1_p2, cdm_8_mark5_1_p4, cdm_8_mark5_1_p5, cdm_8_mark5_1_p6,
       cdm_8_mark5_1_p7, cdm_8_mark5_1_p8, cdm_8_mark5_1_p9, cdm_8_mark5_1_p10, CodeIns, DeepPurple, Main,
       MoveMaker, not_1_out, User;
  wire [7:0] cdm_8_mark5_1_p13, cdm_8_mark5_1_p14;

  // Probe on cdm_8_mark5_1_p1
  // Probe on cdm_8_mark5_1_p4
  // Probe on cdm_8_mark5_1_p2
  // Probe on cdm_8_mark5_1_p5
  // Probe on cdm_8_mark5_1_p7
  // Probe on cdm_8_mark5_1_p8
  // Probe on cdm_8_mark5_1_p6
  // CdM_8_mark5 cdm_8_mark5_1: pin names not known; wires that end beside it: cdm_8_mark5_1_p1, cdm_8_mark5_1_p2, Cl, cdm_8_mark5_1_p4, cdm_8_mark5_1_p5, cdm_8_mark5_1_p6, cdm_8_mark5_1_p7, cdm_8_mark5_1_p8, cdm_8_mark5_1_p9, cdm_8_mark5_1_p10, W_R, out_4, cdm_8_mark5_1_p13, cdm_8_mark5_1_p14
  Decoder #(.disabled(0)) decoder_1 (.out0(CodeIns), .out1(out_8), .sel(cdm_8_mark5_1_p9), .en(cdm_8_mark5_1_p10));
  assign out_5 = not_1_out ? cdm_8_mark5_1_p13 : 8'bz;  // Controlled_Buffer controlled_buffer_1
  not not_1 (not_1_out, W_R);
  assign cdm_8_mark5_1_p14 = W_R ? out_5 : 8'bz;  // Controlled_Buffer controlled_buffer_2
  RAM ram_1 (.addr(out_4), .data(out_5), .sel(RAM), .clk(Cl), .ld(W_R));  // open: clr
  Bank_switch bank_switch_1 (
    .CodeFlag(CodeIns), .Data(out_5), .in_3(out_4), .Storage_flag(out_8), .MoveMaker(MoveMaker), .User(User),
    .Deep_Purple(DeepPurple), .Main(Main), .Cl(Cl));
  assign out_5 = InputData;  // Buffer buffer_1, 8 bits wide
  ROM rom_1 (.addr(out_4), .data(out_5), .sel(Main));
  ROM rom_2 (.addr(out_4), .data(out_5), .sel(DeepPurple));
  ROM rom_3 (.addr(out_4), .data(out_5), .sel(User));
  ROM rom_4 (.addr(out_4), .data(out_5), .sel(MoveMaker));

  assign out_7 = Cl;

  // Other names for the same wires on the sheet: Data[7:0] = out_5; ProcAdr[7:0] = out_4; rd_wr_prime = W_R;
  //   StoreFlag = out_8

  // Notes on the sheet:
  //   STORAGE (RAM)
  //   Main
  //   Deep Purple
  //   User
  //   Move Maker
  //   contents of rom_1 (hex, n*v repeats v):
  //   d0 10 b0 0 e1 f d6 5f d6 78 d0 10 d1 1 a1 d0 13 b0 88 e1 1a d0 16 b0 ee 1d d0 17 b0 0 e0 50 d0 12 d1
  //   40 a1 d0 1 d1 0 7 d2 7 78 ed 37 c2 b2 19 a3 8c c6 ee 2c b2 16 a2 d0 9 d1 0 7 d2 f 78 ed 4c c2 b2 19
  //   a3 8c c6 ee 41 b2 16 a2 d4 ee f9 d2 12 d3 4 ab b1 5 ed 57 d3 0 ab d7 d0 0 d6 52 d0 1 d2 c d3 7 a ed
  //   77 73 e0 73 a1 8a ee 74 8c 8c ee 69 d7 d0 8 d6 52 d0 13 a1 d7 121*0 d1 13 b5 d0 11 a1
  //   contents of rom_2 (hex, n*v repeats v):
  //   d0 12 d3 10 a3 d0 1b d3 ff a3 d0 e d3 8 73 ed 30 b2 a ed 2d c3 d6 41 d1 1a b5 5 e1 22 d6 d8 ee 2c d1
  //   1c a4 d1 1a d2 0 a6 ee 30 c7 88 ee e d0 1c b3 d1 14 a7 d2 0 a2 d1 19 a6 d1 1b a6 ee fa d1 d 76 eb a6
  //   1 c0 d0 f 31 c4 39 ed 88 d3 6 37 ed 81 d1 8 17 73 e1 68 d2 f 3b be 8e 8e d3 19 ae d3 1d ae ee 7f bd
  //   5 e1 7a d2 f 3b be 8e 8e d3 19 ae d3 1d ae ee 7f d1 1d d2 1 a6 ee 86 d1 1d d2 1 a6 ee a4 5 e1 91 d1
  //   1 d6 c7 ee a4 12 b9 5 e1 a4 d1 f 36 b9 5 e0 a1 8d d2 19 a9 d3 1d ad ee c6 3 c0 d0 f 33 c4 3b c0 d0 1
  //   3d ed b9 8c 7 d1 d ee b0 f e1 c2 1 c4 d6 c7 ee c6 d3 1d ac c4 d7 d2 19 ba a e1 d2 d2 1a a8 ee d7 8d
  //   8d d2 1d a9 d7 d1 1d b5 d2 1b bb 77 ed e5 a9 d1 1c a4 d1 1d d2 0 a6 d7 15*0 d0 11 d1 3 a1
  //   contents of rom_3 (hex, n*v repeats v):
  //   d0 15 d2 12 d3 2 ab d6 15 b7 f e1 12 d3 9 ab ee 7 a1 ee fa d3 8 ab b1 5 ed 18 d3 2 ab d3 0 ab d7
  //   215*0 d0 11 d1 3 a1
  //   contents of rom_4 (hex, n*v repeats v):
  //   d0 12 d1 20 a1 d6 38 d2 8 d6 4b 5 ed 13 d6 59 89 ee b d6 1c d0 12 d1 0 a1 ee fa d2 0 d6 4b 7c e0 37
  //   d1 13 b5 89 e1 2e d2 8 3e ee 30 e 32 a ed 35 d6 77 d6 9c d7 d0 13 b0 88 e1 42 d0 14 ee 44 d0 15 b3
  //   bd d2 0 a2 ae d7 d0 13 b0 88 e1 55 d0 f ee 57 d0 7 68 d7 d2 f 7e e4 62 d3 1 ee 6c d2 7 7b e1 6b d3 9
  //   ee 6c 8f 7c e1 73 d6 59 ee 76 be 8e ae d7 be 8a e1 9b e 5 e0 81 d0 f 32 b8 0 ed 9b c0 d0 0 a8 5 e0
  //   91 d0 7 ee 93 d0 f b2 c5 19 8d d2 0 ae a1 d7 d3 1 d1 13 b6 8a 6b 8f a7 d7 84*0 d0 11 d1 0 a1
endmodule

module AI_move (
  input  [7:0] proc_addr,
  input  ram_flag,
  input  [7:0] chain_addr_in,
  input  [7:0] ram_data_in,
  output [7:0] out_5,
  output out_6,
  output [7:0] chain_addr_out,
  output [7:0] out_8,
  output [4:0] out_9,
  output [4:0] out_10,
  output [4:0] Move,
  output [4:0] out_12,
  output [4:0] out_13
);

  wire Adr, and_1_out, comparator_1_eq, Val;

  Increment increment_1 (.value_in(chain_addr_in), .value_out(chain_addr_out));
  Multiplexer #(.width(5), .disabled(0), .enable("false")) multiplexer_1 (
    .in0({5{1'b0}}), .in1({5{1'b1}}), .out(Move), .sel(and_1_out));
  and and_1 (and_1_out, Adr, Val);
  Comparator comparator_1 (.a(proc_addr), .b(8'h14), .eq(comparator_1_eq));  // open: gt, lt
  Comparator comparator_2 (.a(chain_addr_in), .b(ram_data_in), .eq(Val));  // open: gt, lt
  and and_2 (Adr, comparator_1_eq, ram_flag);

  assign out_5 = proc_addr;
  assign out_6 = ram_flag;
  assign out_8 = ram_data_in;
  assign out_9 = Move;
  assign out_10 = Move;
  assign out_12 = Move;
  assign out_13 = Move;
endmodule
