// Logisim project Schemes.circ as structural Verilog: 10 circuits, main circuit Start_Seeds
module main (
);

  wire start_seeds_1_out_11, start_seeds_1_out_12, start_seeds_1_out_13;
  wire [7:0] start_seeds_1_address_2, start_seeds_1_value;

  Start_Seeds start_seeds_1 (
    .Value(start_seeds_1_value), .out_13(start_seeds_1_out_13), .out_12(start_seeds_1_out_12),
    .Address_2(start_seeds_1_address_2), .out_11(start_seeds_1_out_11));  // open: Address, StFlag, Clock, Write_Read, _4, _5, _6, _7, _8
  Increment increment_1 ();  // open: value_in, value_out
  Button_driver button_driver_1 ();  // open: addr_out, addr_in, pos, button, trigger
  Display_driver display_driver_1 ();  // open: addr_field, chain_addr_in, ram_data_in, Cl, addr_field_2, chain_addr_out, ram_data_out, tens, units, is_zero, self_addr, ram_flag, out_13, out_14
  First_move first_move_1 (
    .Address(start_seeds_1_address_2), .StFlag(start_seeds_1_out_11), .Clock(start_seeds_1_out_12),
    .Write_Read(start_seeds_1_out_13), .Data(start_seeds_1_value));  // open: AI, User, out_8, out_10, out_9, Value
  If__4_add_3 if_4_add_3_1 ();  // open: in_1, in_2, in_3, in_4, out_5, out_6, out_7, out_8
  Bin_to_bcd bin_to_bcd_1 ();  // open: in_1, out_2, out_3
  Bcd_to_Bin bcd_to_bin_1 ();  // open: ten_s, one_s, out_3
  WLD wld_1 ();  // open: out_7, End, Address, DatMem, Clock, Write_Read, Data, Doc_Cell
endmodule

module Start_Seeds (
  input  [7:0] Address,
  input  StFlag,
  input  Clock,
  input  Write_Read,
  input  _4,
  input  _5,
  input  _6,
  input  _7,
  input  _8,
  output [7:0] Address_2,
  output out_11,
  output out_12,
  output out_13,
  output [7:0] Value
);

  wire and_3_out, comparator_1_eq, not_1_out, not_2_out, not_3_out, Sel, transistor_1_out;
  wire [7:0] controlled_buffer_1_out, register_1_q;

  Transistor #(.\type ("n")) transistor_1 (.in(1'b0), .out(transistor_1_out), .gate(_4));
  assign controlled_buffer_1_out = _4 ? 8'h4 : 8'bz;  // Controlled_Buffer controlled_buffer_1
  and and_1 (Sel, comparator_1_eq, StFlag, Clock);
  Transistor #(.\type ("n")) transistor_2 (.in(1'b0), .out(transistor_1_out), .gate(_5));
  assign controlled_buffer_1_out = _5 ? 8'h5 : 8'bz;  // Controlled_Buffer controlled_buffer_2
  Transistor #(.\type ("n")) transistor_3 (.in(1'b0), .out(transistor_1_out), .gate(_6));
  assign controlled_buffer_1_out = _6 ? 8'h6 : 8'bz;  // Controlled_Buffer controlled_buffer_3
  not not_1 (not_1_out, comparator_1_eq);
  and and_2 (out_11, not_1_out, StFlag);
  Transistor #(.\type ("n")) transistor_4 (.in(1'b0), .out(transistor_1_out), .gate(_7));
  assign controlled_buffer_1_out = _7 ? 8'h7 : 8'bz;  // Controlled_Buffer controlled_buffer_4
  Pull_Resistor #(.pull(1)) pull_resistor_1 (.node(transistor_1_out));
  Transistor #(.\type ("n")) transistor_5 (.in(1'b0), .out(transistor_1_out), .gate(_8));
  assign controlled_buffer_1_out = _8 ? 8'h8 : 8'bz;  // Controlled_Buffer controlled_buffer_5
  Comparator #(.mode("unsigned")) comparator_1 (.a(Address), .b({8{1'b0}}), .eq(comparator_1_eq));  // open: gt, lt
  not not_2 (not_2_out, not_3_out);
  not not_3 (not_3_out, transistor_1_out);
  assign Value = and_3_out ? register_1_q : 8'bz;  // Controlled_Buffer controlled_buffer_6
  Register #(.trigger("falling")) register_1 (
    .D(controlled_buffer_1_out), .Q(register_1_q), .clk(not_2_out));  // open: en, clr
  and and_3 (and_3_out, Sel, Write_Read);

  assign Address_2 = Address;
  assign out_12 = Clock;
  assign out_13 = Write_Read;

  // Other names for the same wires on the sheet: In_Out = Write_Read
endmodule

module Bin_to_bcd (
  input  [7:0] in_1,
  output [3:0] out_2,
  output [3:0] out_3
);

  wire if_4_add_3_1_out_5, if_4_add_3_1_out_6, if_4_add_3_1_out_7, if_4_add_3_1_out_8, if_4_add_3_2_out_5,
       if_4_add_3_2_out_6, if_4_add_3_2_out_7, if_4_add_3_2_out_8, if_4_add_3_3_out_6, if_4_add_3_3_out_7,
       if_4_add_3_3_out_8, if_4_add_3_5_out_5, if_4_add_3_5_out_6, if_4_add_3_5_out_7, if_4_add_3_5_out_8,
       if_4_add_3_6_out_5, if_4_add_3_6_out_6, if_4_add_3_6_out_7, if_4_add_3_6_out_8;

  If__4_add_3 if_4_add_3_1 (
    .in_1(1'b0), .in_2(in_1[7]), .in_3(in_1[6]), .in_4(in_1[5]), .out_5(if_4_add_3_1_out_5),
    .out_6(if_4_add_3_1_out_6), .out_7(if_4_add_3_1_out_7), .out_8(if_4_add_3_1_out_8));
  If__4_add_3 if_4_add_3_2 (
    .in_1(if_4_add_3_1_out_6), .in_2(if_4_add_3_1_out_7), .in_3(if_4_add_3_1_out_8), .in_4(in_1[4]),
    .out_5(if_4_add_3_2_out_5), .out_6(if_4_add_3_2_out_6), .out_7(if_4_add_3_2_out_7),
    .out_8(if_4_add_3_2_out_8));
  If__4_add_3 if_4_add_3_3 (
    .in_1(1'b0), .in_2(if_4_add_3_1_out_5), .in_3(if_4_add_3_2_out_5), .in_4(if_4_add_3_5_out_5),
    .out_6(if_4_add_3_3_out_6), .out_7(if_4_add_3_3_out_7), .out_8(if_4_add_3_3_out_8));  // open: out_5
  If__4_add_3 if_4_add_3_4 (
    .in_1(if_4_add_3_3_out_6), .in_2(if_4_add_3_3_out_7), .in_3(if_4_add_3_3_out_8),
    .in_4(if_4_add_3_6_out_5), .out_6(out_2[3]), .out_7(out_2[2]), .out_8(out_2[1]));  // open: out_5
  If__4_add_3 if_4_add_3_5 (
    .in_1(if_4_add_3_2_out_6), .in_2(if_4_add_3_2_out_7), .in_3(if_4_add_3_2_out_8), .in_4(in_1[3]),
    .out_5(if_4_add_3_5_out_5), .out_6(if_4_add_3_5_out_6), .out_7(if_4_add_3_5_out_7),
    .out_8(if_4_add_3_5_out_8));
  If__4_add_3 if_4_add_3_6 (
    .in_1(if_4_add_3_5_out_6), .in_2(if_4_add_3_5_out_7), .in_3(if_4_add_3_5_out_8), .in_4(in_1[2]),
    .out_5(if_4_add_3_6_out_5), .out_6(if_4_add_3_6_out_6), .out_7(if_4_add_3_6_out_7),
    .out_8(if_4_add_3_6_out_8));
  If__4_add_3 if_4_add_3_7 (
    .in_1(if_4_add_3_6_out_6), .in_2(if_4_add_3_6_out_7), .in_3(if_4_add_3_6_out_8), .in_4(in_1[1]),
    .out_5(out_2[0]), .out_6(out_3[3]), .out_7(out_3[2]), .out_8(out_3[1]));

  assign out_3[0] = in_1[0];
endmodule

module If__4_add_3 (
  input  in_1,
  input  in_2,
  input  in_3,
  input  in_4,
  output out_5,
  output out_6,
  output out_7,
  output out_8
);

  wire comparator_1_gt;
  wire [3:0] adder_1_out;

  Comparator #(.width(4), .mode("unsigned")) comparator_1 (
    .a({in_1, in_2, in_3, in_4}), .b(4'b0100), .gt(comparator_1_gt));  // open: eq, lt
  Adder #(.width(4)) adder_1 (.a({in_1, in_2, in_3, in_4}), .b(4'b0011), .out(adder_1_out));  // open: cin, cout
  Multiplexer #(.width(4), .enable("false")) multiplexer_1 (
    .in0({in_1, in_2, in_3, in_4}), .in1(adder_1_out), .out({out_5, out_6, out_7, out_8}),
    .sel(comparator_1_gt));
endmodule

module Bcd_to_Bin (
  input  [3:0] ten_s,
  input  [3:0] one_s,
  output [7:0] out_3
);

  wire [7:0] multiplier_1_out;

  Multiplier multiplier_1 (.a({4'b0000, ten_s}), .b(8'ha), .out(multiplier_1_out));  // open: cin, cout
  Adder adder_1 (.a({4'b0000, one_s}), .b(multiplier_1_out), .out(out_3));  // open: cin, cout
endmodule

module Button_driver (
  input  [7:0] pos,
  input  [7:0] addr_in,
  input  button,
  output [7:0] addr_out,
  output trigger
);

  assign addr_in = button ? pos : 8'bz;  // Controlled_Buffer controlled_buffer_1
  Transistor #(.\type ("n")) transistor_1 (.in(1'b1), .out(trigger), .gate(button));

  assign addr_out = addr_in;
endmodule

module Increment (
  input  [7:0] value_in,
  output [7:0] value_out
);

  Adder adder_1 (.a(value_in), .b(8'h1), .out(value_out));  // open: cin, cout
endmodule

module Display_driver (
  input  [7:0] chain_addr_in,
  input  [7:0] addr_field,
  input  [7:0] ram_data_in,
  input  Cl,
  input  ram_flag,
  output [7:0] chain_addr_out,
  output [7:0] self_addr,
  output [7:0] addr_field_2,
  output [7:0] ram_data_out,
  output [3:0] tens,
  output [3:0] units,
  output is_zero,
  output out_13,
  output out_14
);

  wire and_1_out, comparator_1_eq, is_our_addr, not_1_out;
  wire [7:0] register_1_q;

  Increment increment_1 (.value_in(chain_addr_in), .value_out(chain_addr_out));
  Register register_1 (.D(ram_data_in), .en(and_1_out), .Q(register_1_q), .clk(Cl));  // open: clr
  and and_1 (and_1_out, is_our_addr, ram_flag);
  Comparator comparator_1 (.a(register_1_q), .b({8{1'b0}}), .eq(comparator_1_eq));  // open: gt, lt
  Comparator comparator_2 (.a(chain_addr_out), .b(addr_field), .eq(is_our_addr));  // open: gt, lt
  Bin_to_bcd bin_to_bcd_1 (.in_1(register_1_q), .out_2(tens), .out_3(units));
  assign is_zero = not_1_out ? 1'b0 : 1'bz;  // Controlled_Buffer controlled_buffer_1
  not not_1 (not_1_out, comparator_1_eq);

  assign addr_field_2 = addr_field;
  assign out_13 = Cl;
  assign out_14 = ram_flag;
  assign ram_data_out = ram_data_in;
  assign self_addr = chain_addr_out;
endmodule

module First_move (
  input  [7:0] Address,
  input  StFlag,
  input  Clock,
  input  Write_Read,
  input  [7:0] Data,
  input  AI,
  input  User,
  output [7:0] out_8,
  output out_9,
  output out_10,
  output [7:0] Value
);

  wire and_3_out, comparator_1_eq, not_1_out, not_2_out, not_3_out, Sel, transistor_1_out;
  wire [7:0] controlled_buffer_1_out, register_1_q;

  and and_1 (Sel, comparator_1_eq, StFlag, Clock);
  Transistor #(.\type ("n")) transistor_1 (.in(1'b0), .out(transistor_1_out), .gate(AI));
  assign controlled_buffer_1_out = AI ? 8'h1 : 8'bz;  // Controlled_Buffer controlled_buffer_1
  Pull_Resistor #(.pull(1)) pull_resistor_1 (.node(transistor_1_out));
  Transistor #(.\type ("n")) transistor_2 (.in(1'b0), .out(transistor_1_out), .gate(User));
  assign controlled_buffer_1_out = User ? 8'h2 : 8'bz;  // Controlled_Buffer controlled_buffer_2
  not not_1 (not_1_out, comparator_1_eq);
  and and_2 (out_9, not_1_out, StFlag);
  not not_2 (not_2_out, transistor_1_out);
  not not_3 (not_3_out, not_2_out);
  Multiplexer #(.width(8), .enable("false")) multiplexer_1 (
    .in0(Data), .in1(register_1_q), .out(Value), .sel(and_3_out));
  Register #(.trigger("falling")) register_1 (
    .D(controlled_buffer_1_out), .Q(register_1_q), .clk(not_3_out));  // open: en, clr
  and and_3 (and_3_out, Sel, Write_Read);
  Comparator #(.mode("unsigned")) comparator_1 (.a(Address), .b(8'h8), .eq(comparator_1_eq));  // open: gt, lt

  assign out_8 = Address;
  assign out_10 = Write_Read;

  // Other names for the same wires on the sheet: In_Out = Write_Read
endmodule

module WLD (
  input  [7:0] Doc_Cell,
  input  [7:0] Address,
  input  DatMem,
  input  Clock,
  input  End,
  input  Write_Read,
  output out_7,
  output [7:0] Data
);

  wire and_3_out, comparator_1_eq, not_1_out, Sel;

  and and_1 (Sel, comparator_1_eq, DatMem, Clock);
  not not_1 (not_1_out, comparator_1_eq);
  and and_2 (out_7, not_1_out, DatMem);
  assign Data = and_3_out ? {{7{1'b0}}, End} : 8'bz;  // Controlled_Buffer controlled_buffer_1
  and and_3 (and_3_out, Sel, Write_Read);
  Comparator #(.mode("unsigned")) comparator_1 (.a(Address), .b(Doc_Cell), .eq(comparator_1_eq));  // open: gt, lt
endmodule
